# Fritzing sketch master (saved by Fritzing 0.9.3b)
breadboards: 1

parts:
  U1 = atmega328 [package=dip]
  U2 = MAX485 [package=dil08]

nets:
  N1: U1.D9_(PWM), U2.RE, U2.DE
  N2: U1.D10_(PWM), U2.RO
  N3: U1.D11_(PWM), U2.DI
  N4: U1.AVCC, U2.VCC
  GND: U1.GND, U2.GND
