# Fritzing sketch relayM (saved by Fritzing 0.9.3b)
breadboards: 1

parts:
  U1 = atmega328 [package=dip]
  U2 = MAX485 [package=dil08]
  Q1 = npn-Powertransistor [package="TO220 [THT]"]
  U3 = RELAY [package=relay-t9a]
  R1 = Resistor [tolerance=±5% resistance=1k package="0603 [SMD]"]
  D1 = Zener Diode [part_number=1N4732A breakdown_voltage=3.6V package="Melf DO-213 AB [SMD]"]
  XTAL1 = Crystal [frequency="16 Mhz" package=SMD]

nets:
  N1: U1.VCC, U3.COIL1, D1.cathode
  N2: U1.XLAT1, XTAL1.pin_1
  N3: U1.XLAT2, XTAL1.pin_0
  N4: U1.D8, R1.Pin_1
  N5: U1.D9_(PWM), U2.RE, U2.DE
  N6: U1.D10_(PWM), U2.RO
  N7: U1.D11_(PWM), U2.DI
  N8: U1.AVCC, U2.VCC
  GND: U1.GND, U2.GND, Q1.emitter
  N9: Q1.base, R1.Pin_0
  N10: U3.COIL2, D1.anode
